# Fritzing sketch TiefpassAktiv (saved by Fritzing 1.0.2b)
breadboards: 1

parts:
  IC1 = TL072 [package="DIP (Dual Inline) [THT]"]
  IC1_PWR = TL072 [package="DIP (Dual Inline) [THT]"]  # not connected
  IC1_A = TL072 [package="DIP (Dual Inline) [THT]"]  # not connected
  IC1_B = TL072 [package="DIP (Dual Inline) [THT]"]  # not connected
  C1 = Ceramic Capacitor [capacitance=100nF voltage=35V package="100 mil [THT, multilayer]"]
  R1 = Resistor [tolerance=±5% power=0.25 resistance=10k package=THT]
  C2 = Ceramic Capacitor [capacitance=100nF voltage=35V package="100 mil [THT, multilayer]"]
  R2 = Resistor [tolerance=±5% power=0.25 resistance=10k package=THT]
  C3 = Electrolytic Capacitor [capacitance=1µF voltage=35V package="100 mil [THT, electrolytic]"]
  C4 = Electrolytic Capacitor [capacitance=1µF voltage=35V package="100 mil [THT, electrolytic]"]

nets:
  N1: IC1.connector0, R1.Pin_1, C2.1
  N2: IC1.connector1, R1.Pin_0, C2.0, R2.Pin_0
  N3: IC1.connector2, C3.-, C4.+
  N4: IC1.connector3, C1.0, C3.+
  N5: IC1.connector7, C1.1, C4.-

custom parts:
  TL072: Dual Operational Amplifier
  TL072: Dual Operational Amplifier
  TL072: Dual Operational Amplifier
  TL072: Dual Operational Amplifier
